# Fritzing sketch Spannung und Strom Messen 2024-11-20 (saved by Fritzing 1.0.0rc)
circuit board: 7.92cm x 4.6cm
breadboards: 1

parts:
  Jumper = female pin header, 2 pins [form="♀ (female)"]
  Widerstand_330_Ohm = Resistor [tolerance=±5% power=0.25W resistance=330 package=THT]
  LED_Rot = LED - 5mm [color="Red (633nm)" current=0.030A package="5 mm [THT]"]
  9V = Battery block 9V  # not connected
  Klemme = Screw terminal - 2 pins [package=THT]

nets:
  N1: Jumper.pin1, LED_Rot.cathode
  N2: Jumper.pin2, Klemme.pin2
  N3: Widerstand_330_Ohm.Pin_0, Klemme.pin1
  N4: Widerstand_330_Ohm.Pin_1, LED_Rot.anode

notes:
  Spannung und Strom messen
  -
  +9V
  ver.2024-11-20 by DM9GP
  GND
  +
